// Logisim project ETI_7_2.circ as structural Verilog: 1 circuit, main circuit main
module main (
);

  wire and_1_out, and_2_out, and_3_out, and_4_out, and_5_out, and_6_out, and_7_out, and_8_out, and_9_out,
       and_10_out, and_11_out, and_12_out, and_13_out, and_14_out, and_15_out, and_16_out, and_17_out,
       and_18_out, and_19_out, and_20_out, and_21_out, and_22_out, and_23_out, and_24_out, and_25_out,
       and_26_out, and_27_out, and_28_out, and_29_out, and_30_out, and_31_out, and_32_out, and_33_out,
       and_34_out, and_35_out, and_36_out, and_37_out, and_38_out, and_39_out, and_40_out, and_41_out,
       and_42_out, and_43_out, and_44_out, and_45_out, and_46_out, and_47_out, and_48_out, and_49_out,
       and_50_out, and_51_out, and_52_out, and_53_out, and_54_out, and_55_out, and_56_out, and_57_out,
       and_58_out, and_59_out, and_60_out, and_61_out, and_62_out, and_63_out, and_64_out, and_65_out,
       and_66_out, and_67_out, and_68_out, and_69_out, and_70_out, and_71_out, and_72_out, and_73_out,
       button_1_out, button_2_out, clock_1_out, clock_2_out, d_ff_1_q, d_ff_1_qn, d_ff_2_q, d_ff_2_qn,
       d_ff_3_q, d_ff_3_qn, d_ff_4_q, d_ff_4_qn, d_ff_5_q, d_ff_5_qn, d_ff_6_q, d_ff_6_qn, d_ff_7_q,
       d_ff_7_qn, d_ff_8_q, d_ff_8_qn, or_1_out, or_2_out, or_3_out, or_4_out, or_5_out, or_6_out, or_7_out,
       or_8_out, or_9_out, or_10_out, or_11_out, or_12_out, or_13_out, or_14_out, or_15_out, or_16_out,
       or_17_out, or_18_out, or_19_out, or_20_out;

  Clock clock_1 (.out(clock_1_out));
  Clock clock_2 (.out(clock_2_out));
  Button button_1 (.out(button_1_out));
  D_Flip_Flop d_ff_1 (
    .clk(clock_1_out), .D(d_ff_1_qn), .Q(d_ff_1_q), .Qn(d_ff_1_qn), .reset(button_1_out));  // open: preset, en
  D_Flip_Flop d_ff_2 (
    .clk(clock_1_out), .D(or_5_out), .Q(d_ff_2_q), .Qn(d_ff_2_qn), .reset(button_1_out));  // open: preset, en
  D_Flip_Flop d_ff_3 (
    .clk(clock_1_out), .D(or_3_out), .Q(d_ff_3_q), .Qn(d_ff_3_qn), .reset(button_1_out));  // open: preset, en
  D_Flip_Flop d_ff_4 (
    .clk(clock_1_out), .D(or_1_out), .Q(d_ff_4_q), .Qn(d_ff_4_qn), .reset(button_1_out));  // open: preset, en
  Button button_2 (.out(button_2_out));
  D_Flip_Flop d_ff_5 (
    .clk(clock_2_out), .D(d_ff_5_qn), .Q(d_ff_5_q), .Qn(d_ff_5_qn), .preset(1'b0), .reset(button_2_out));  // open: en
  D_Flip_Flop d_ff_6 (
    .clk(clock_2_out), .D(or_6_out), .Q(d_ff_6_q), .Qn(d_ff_6_qn), .preset(button_2_out), .reset(1'b0));  // open: en
  D_Flip_Flop d_ff_7 (
    .clk(clock_2_out), .D(or_4_out), .Q(d_ff_7_q), .Qn(d_ff_7_qn), .preset(button_2_out), .reset(1'b0));  // open: en
  D_Flip_Flop d_ff_8 (
    .clk(clock_2_out), .D(or_2_out), .Q(d_ff_8_q), .Qn(d_ff_8_qn), .preset(1'b0), .reset(button_2_out));  // open: en
  and and_1 (and_1_out, d_ff_4_qn, d_ff_3_q, d_ff_2_q, d_ff_1_qn);
  and and_2 (and_2_out, d_ff_3_q, d_ff_2_qn, d_ff_1_q);
  or or_1 (or_1_out, and_2_out, and_1_out, and_5_out, and_6_out);
  and and_3 (and_3_out, d_ff_8_qn, d_ff_7_q, d_ff_6_q, d_ff_5_qn);
  and and_4 (and_4_out, d_ff_7_q, d_ff_6_qn, d_ff_5_q);
  or or_2 (or_2_out, and_4_out, and_3_out, and_8_out, and_7_out);
  and and_5 (and_5_out, d_ff_4_q, d_ff_3_qn);
  and and_6 (and_6_out, d_ff_4_q, d_ff_2_qn);
  and and_7 (and_7_out, d_ff_8_q, d_ff_6_qn);
  and and_8 (and_8_out, d_ff_8_q, d_ff_7_qn);
  and and_9 (and_9_out, d_ff_3_qn, d_ff_1_q);
  and and_10 (and_10_out, d_ff_3_qn, d_ff_2_q);
  and and_11 (and_11_out, d_ff_3_q, d_ff_2_qn, d_ff_1_qn);
  or or_3 (or_3_out, and_9_out, and_10_out, and_11_out);
  and and_12 (and_12_out, d_ff_7_q, d_ff_6_qn, d_ff_5_qn);
  and and_13 (and_13_out, d_ff_7_qn, d_ff_5_q);
  and and_14 (and_14_out, d_ff_7_qn, d_ff_6_q);
  or or_4 (or_4_out, and_13_out, and_14_out, and_12_out);
  and and_15 (and_15_out, d_ff_3_qn, d_ff_2_q, d_ff_1_q);
  and and_16 (and_16_out, d_ff_2_qn, d_ff_1_qn);
  or or_5 (or_5_out, and_16_out, and_15_out, and_19_out);
  and and_17 (and_17_out, d_ff_6_qn, d_ff_5_qn);
  and and_18 (and_18_out, d_ff_7_qn, d_ff_6_q, d_ff_5_q);
  or or_6 (or_6_out, and_17_out, and_18_out, and_20_out);
  and and_19 (and_19_out, d_ff_4_q, d_ff_3_q, d_ff_1_q);
  and and_20 (and_20_out, d_ff_8_q, d_ff_7_q, d_ff_5_q);
  and and_21 (and_21_out, d_ff_4_qn, d_ff_3_q, d_ff_2_q, d_ff_1_qn);
  and and_22 (and_22_out, d_ff_4_q, d_ff_2_q, d_ff_1_q);
  or or_7 (or_7_out, and_21_out, and_22_out);
  _7_Segment_Display u_7_segment_display_1 (
    .g(or_19_out), .f(or_17_out), .a(or_7_out), .b(or_9_out), .e(or_15_out), .d(or_14_out), .c(or_12_out));  // open: dp
  and and_23 (and_23_out, d_ff_8_q, d_ff_7_q, d_ff_6_qn);
  and and_24 (and_24_out, d_ff_8_qn, d_ff_7_qn, d_ff_6_qn);
  and and_25 (and_25_out, d_ff_8_qn, d_ff_6_qn, d_ff_5_q);
  or or_8 (or_8_out, and_25_out, and_23_out);
  _7_Segment_Display u_7_segment_display_2 (
    .g(or_20_out), .f(or_18_out), .a(or_8_out), .b(or_10_out), .e(or_16_out), .d(or_13_out), .c(or_11_out));  // open: dp
  and and_26 (and_26_out, d_ff_3_qn, d_ff_2_q, d_ff_1_q);
  and and_27 (and_27_out, d_ff_4_qn, d_ff_3_q, d_ff_2_qn, d_ff_1_qn);
  or or_9 (or_9_out, and_26_out, and_27_out, and_30_out, and_31_out);
  and and_28 (and_28_out, d_ff_6_qn, d_ff_5_q);
  and and_29 (and_29_out, d_ff_8_q, d_ff_6_q, d_ff_5_qn);
  or or_10 (or_10_out, and_24_out, and_28_out, and_29_out);
  and and_30 (and_30_out, d_ff_4_q, d_ff_3_qn, d_ff_1_qn);
  and and_31 (and_31_out, d_ff_4_q, d_ff_3_q, d_ff_1_q);
  and and_32 (and_32_out, d_ff_6_qn, d_ff_5_q);
  and and_33 (and_33_out, d_ff_8_qn, d_ff_7_qn, d_ff_6_qn);
  and and_34 (and_34_out, d_ff_8_q, d_ff_7_qn, d_ff_6_q);
  or or_11 (or_11_out, and_33_out, and_32_out, and_34_out, and_38_out);
  and and_35 (and_35_out, d_ff_4_qn, d_ff_3_q, d_ff_2_qn);
  and and_36 (and_36_out, d_ff_3_qn, d_ff_2_q, d_ff_1_q);
  and and_37 (and_37_out, d_ff_4_q, d_ff_3_qn, d_ff_1_qn);
  or or_12 (or_12_out, and_36_out, and_35_out, and_37_out, and_41_out);
  and and_38 (and_38_out, d_ff_8_q, d_ff_6_q, d_ff_5_qn);
  and and_39 (and_39_out, d_ff_8_qn, d_ff_7_qn, d_ff_6_qn);
  and and_40 (and_40_out, d_ff_2_qn, d_ff_1_q);
  and and_41 (and_41_out, d_ff_4_q, d_ff_3_q, d_ff_1_q);
  and and_42 (and_42_out, d_ff_8_q, d_ff_6_q);
  and and_43 (and_43_out, d_ff_7_q, d_ff_5_q);
  and and_44 (and_44_out, d_ff_8_qn, d_ff_7_qn, d_ff_5_qn);
  or or_13 (or_13_out, and_39_out, and_44_out, and_43_out, and_42_out, and_48_out);
  and and_45 (and_45_out, d_ff_4_q, d_ff_2_qn);
  and and_46 (and_46_out, d_ff_4_q, d_ff_1_q);
  and and_47 (and_47_out, d_ff_4_qn, d_ff_3_q, d_ff_1_qn);
  or or_14 (or_14_out, and_40_out, and_47_out, and_45_out, and_46_out);
  and and_48 (and_48_out, d_ff_8_q, d_ff_7_q);
  and and_49 (and_49_out, d_ff_8_qn, d_ff_6_qn);
  and and_50 (and_50_out, d_ff_3_q, d_ff_1_qn);
  and and_51 (and_51_out, d_ff_4_qn, d_ff_2_qn);
  or or_15 (or_15_out, and_51_out, and_50_out, and_56_out);
  and and_52 (and_52_out, d_ff_8_qn, d_ff_5_qn);
  and and_53 (and_53_out, d_ff_7_q, d_ff_6_qn);
  and and_54 (and_54_out, d_ff_7_q, d_ff_5_q);
  or or_16 (or_16_out, and_49_out, and_52_out, and_53_out, and_54_out, and_59_out);
  and and_55 (and_55_out, d_ff_4_qn, d_ff_3_qn, d_ff_2_qn);
  and and_56 (and_56_out, d_ff_4_q, d_ff_1_q);
  and and_57 (and_57_out, d_ff_2_qn, d_ff_1_q);
  and and_58 (and_58_out, d_ff_8_qn, d_ff_6_qn, d_ff_5_q);
  and and_59 (and_59_out, d_ff_8_q, d_ff_7_qn, d_ff_6_q);
  and and_60 (and_60_out, d_ff_4_q, d_ff_1_q);
  and and_61 (and_61_out, d_ff_4_qn, d_ff_3_q, d_ff_2_q, d_ff_1_qn);
  or or_17 (or_17_out, and_55_out, and_57_out, and_61_out, and_60_out, and_65_out);
  and and_62 (and_62_out, d_ff_8_q, d_ff_7_qn, d_ff_6_q);
  and and_63 (and_63_out, d_ff_7_q, d_ff_5_q);
  and and_64 (and_64_out, d_ff_8_qn, d_ff_6_q, d_ff_5_qn);
  or or_18 (or_18_out, and_58_out, and_64_out, and_63_out, and_62_out, and_67_out);
  and and_65 (and_65_out, d_ff_4_q, d_ff_3_q, d_ff_2_qn);
  and and_66 (and_66_out, d_ff_4_qn, d_ff_2_qn, d_ff_1_qn);
  and and_67 (and_67_out, d_ff_8_q, d_ff_7_q, d_ff_6_qn);
  and and_68 (and_68_out, d_ff_8_qn, d_ff_6_qn, d_ff_5_qn);
  and and_69 (and_69_out, d_ff_4_qn, d_ff_3_qn, d_ff_2_q, d_ff_1_q);
  and and_70 (and_70_out, d_ff_3_q, d_ff_2_q, d_ff_1_qn);
  or or_19 (or_19_out, and_66_out, and_69_out, and_70_out);
  and and_71 (and_71_out, d_ff_7_q, d_ff_6_qn, d_ff_5_qn);
  and and_72 (and_72_out, d_ff_8_q, d_ff_6_qn, d_ff_5_q);
  and and_73 (and_73_out, d_ff_8_qn, d_ff_7_q, d_ff_5_qn);
  or or_20 (or_20_out, and_68_out, and_73_out, and_71_out, and_72_out);

  // Notes on the sheet:
  //   D
  //   C
  //   B
  //   A
  //   D
  //   C
  //   B
  //   A
  //   Bonus Aufgabe
endmodule
