// Logisim project Helloworld.circ as structural Verilog: 1 circuit, main circuit main
module main (
);

  wire and_1_out, and_2_out, and_3_out, and_4_out, and_5_out, and_6_out, and_7_out, and_8_out, and_9_out,
       and_10_out, and_11_out, clock_1_out, clock_2_out, clock_3_out, not_1_out, not_2_out, not_3_out,
       or_1_out, or_2_out, or_3_out, or_4_out, or_5_out;

  Clock #(.highDuration(4), .lowDuration(4)) clock_1 (.out(clock_1_out));
  Clock #(.highDuration(2), .lowDuration(2)) clock_2 (.out(clock_2_out));
  not not_1 (not_1_out, clock_1_out);
  not not_2 (not_2_out, clock_2_out);
  Clock clock_3 (.out(clock_3_out));
  not not_3 (not_3_out, clock_3_out);
  and and_1 (and_1_out, clock_3_out, not_1_out);
  and and_2 (and_2_out, clock_3_out, clock_2_out);
  and and_3 (and_3_out, clock_3_out, clock_2_out);
  and and_4 (and_4_out, not_3_out, not_2_out);
  and and_5 (and_5_out, not_3_out, clock_1_out);
  and and_6 (and_6_out, clock_3_out, not_1_out);
  and and_7 (and_7_out, not_3_out, clock_1_out);
  and and_8 (and_8_out, not_3_out, not_2_out);
  and and_9 (and_9_out, not_2_out, not_1_out);
  and and_10 (and_10_out, clock_2_out, clock_1_out);
  and and_11 (and_11_out, clock_3_out, clock_1_out);
  or or_1 (or_1_out, and_1_out, and_2_out);
  or or_2 (or_2_out, and_3_out, and_4_out, and_5_out);
  or or_3 (or_3_out, clock_2_out, and_6_out, and_7_out);
  or or_4 (or_4_out, not_1_out, and_8_out);
  or or_5 (or_5_out, and_9_out, and_10_out, and_11_out);
  _7_Segment_Display u_7_segment_display_1 (
    .g(or_5_out), .f(or_4_out), .a(or_1_out), .b(or_2_out), .e(1'b1), .d(or_3_out), .c(or_2_out));  // open: dp

  // Notes on the sheet:
  //   x_2
  //   x_1
  //   x_0
  //   a
  //   b, c
  //   d
  //   e
  //   f
  //   g
endmodule
