// Logisim project Tut2.circ as structural Verilog: 1 circuit, main circuit main
module main (
);

  wire and_1_out, and_2_out, and_3_out, not_1_out, not_2_out, or_1_out, x_0_out, x_1_out;

  Clock x_0 (.out(x_0_out));
  Clock x_1 (.out(x_1_out));
  not not_1 (not_1_out, x_0_out);
  not not_2 (not_2_out, x_1_out);
  and and_1 (and_1_out, x_0_out, not_2_out);
  and and_2 (and_2_out, x_1_out, not_1_out);
  and and_3 (and_3_out, and_1_out, and_2_out);
  or or_1 (or_1_out, and_3_out, 1'b1);
  LED led_1 (.in(or_1_out));
endmodule
