// Logisim project 4Vars.circ as structural Verilog: 1 circuit, main circuit main
module main (
);

  wire and_1_out, not_1_out, not_2_out, not_3_out, not_4_out, or_1_out, or_2_out, or_3_out, or_4_out,
       or_5_out, x_1_out, x_2_out, x_3_out, x_4_out;

  Clock #(.highDuration(8), .lowDuration(8)) x_4 (.out(x_4_out));
  not not_1 (not_1_out, x_4_out);
  Clock #(.highDuration(2), .lowDuration(2)) x_2 (.out(x_2_out));
  Clock #(.highDuration(4), .lowDuration(4)) x_3 (.out(x_3_out));
  not not_2 (not_2_out, x_3_out);
  not not_3 (not_3_out, x_2_out);
  Clock x_1 (.out(x_1_out));
  not not_4 (not_4_out, x_1_out);
  // OR_Gate or_1 has open pins: out=or_1_out
  // OR_Gate or_2 has open pins: out=or_2_out
  // OR_Gate or_3 has open pins: out=or_3_out
  // OR_Gate or_4 has open pins: out=or_4_out
  // OR_Gate or_5 has open pins: out=or_5_out
  and and_1 (and_1_out, or_1_out, or_2_out, or_3_out, or_4_out, or_5_out);
  LED f (.in(and_1_out));
endmodule
