// Logisim project circle.circ as structural Verilog: 1 circuit, main circuit main
module main (
);

  wire and_1_out, and_2_out, and_3_out, and_4_out, clock_1_out, Q1_2_q, Q1_2_qn, Q1_q, Q1_qn;

  Clock clock_1 (.out(clock_1_out));
  J_K_Flip_Flop Q1 (.J(1'b1), .clk(clock_1_out), .K(1'b1), .Q(Q1_q), .Qn(Q1_qn));  // open: preset, en, reset
  J_K_Flip_Flop Q1_2 (.J(Q1_q), .clk(clock_1_out), .K(Q1_q), .Q(Q1_2_q), .Qn(Q1_2_qn));  // open: preset, en, reset
  and and_1 (and_1_out, Q1_qn, Q1_2_qn);
  and and_2 (and_2_out, Q1_q, Q1_2_qn);
  and and_3 (and_3_out, Q1_qn, Q1_2_q);
  and and_4 (and_4_out, Q1_q, Q1_2_q);
  _7_Segment_Display u_7_segment_display_1 (
    .g(and_3_out), .e(and_4_out), .d(and_1_out), .c(and_2_out));  // open: f, a, b, dp
endmodule
