// Logisim project example.circ as structural Verilog: 1 circuit, main circuit main
module main (
);

  wire and_1_out, clock_1_out, clock_2_out;

  Clock clock_1 (.out(clock_1_out));
  Clock clock_2 (.out(clock_2_out));
  LED led_1 (.in(and_1_out));
  and and_1 (and_1_out, clock_2_out, clock_1_out, 1'b1);
endmodule
